# Fritzing sketch blink_neopixels_number (saved by Fritzing 0.8.7b)

parts:
  LED1 = Adafruit_FLORA_RGB_Smart_Pixel
  LED2 = Adafruit_FLORA_RGB_Smart_Pixel
  LED3 = Adafruit_FLORA_RGB_Smart_Pixel
  GEMMA1 = Adafruit GEMMA

nets:
  N1: LED1.connector1, LED2.connector1, LED3.connector1, GEMMA1.Vout
  N2: LED1.connector2, GEMMA1.D1
  N3: LED1.connector3, LED2.connector3, LED3.connector3, GEMMA1.GND
  N4: LED1.connector4, LED2.connector2
  N5: LED2.connector4, LED3.connector2

custom parts:
  Adafruit GEMMA: Adafruit Gemma wearable electronics main board.
