# Fritzing sketch traffic_light (saved by Fritzing 0.8.7b)
breadboards: 1

parts:
  GEMMA1 = Adafruit GEMMA
  LED1 = Adafruit_FLORA_RGB_Smart_Pixel
  S1 = Toggle Switch [package=THT]
  R1 = Resistor [tolerance=±5% resistance=220 package=THT]

nets:
  N1: GEMMA1.GND, LED1.connector3, R1.Pin_1
  N2: GEMMA1.Vout, LED1.connector1, S1.COM
  N3: GEMMA1.D0, LED1.connector2
  N4: GEMMA1.D2/A1, S1.L2, R1.Pin_0

custom parts:
  Adafruit GEMMA: Adafruit Gemma wearable electronics main board.
